# Fritzing sketch 1 valvula - realista (saved by Fritzing 0.9.1b)
circuit board: 4.29402cm x 2.50721cm
breadboards: 1

parts:
  12V1 = Power plug
  LED2 = LED - 3mm [color="Yellow (595nm)" package="3 mm [THT]"]
  R8 = Resistor [tolerance=±5% resistance=1.2k package=THT]
  Optocouple1 = IC, DIP package, 4 pins [chip_label=IC]
  R9 = Resistor [tolerance=±5% resistance=1k package=THT]
  R10 = Resistor [tolerance=±5% resistance=1k power=250mW package=THT]
  D2 = Rectifier Diode [part_number=1N4001 package="300 mil [THT]"]
  Valvula_12V = screw terminal, 2 pins
  Q3 = npn-Powertransistor [package="TO220 [THT]"]
  J1 = Screw terminal - 2 pins [package=THT]
  R11 = Resistor [tolerance=±5% resistance=1k power=250mW package=THT]
  R12 = Resistor [tolerance=±5% resistance=1k package=THT]

nets:
  GND: 12V1.GND, Q3.emitter
  N1: 12V1.VCC, R8.Pin_1, Optocouple1.pin4, D2.cathode, Valvula_12V.pin2
  N2: LED2.cathode, D2.anode, Valvula_12V.pin1, Q3.collector
  N3: LED2.anode, R8.Pin_0
  N4: Optocouple1.pin1, R11.Pin_0
  N5: Optocouple1.pin2, J1.pin1
  N6: Optocouple1.pin3, R9.Pin_0
  N7: R9.Pin_1, R12.Pin_1
  N8: R10.Pin_0, J1.pin2
  N9: R10.Pin_1, R11.Pin_1
  N10: Q3.base, R12.Pin_0

notes:
  320mA
  7.2mA
  R8: 0.077W
  LED2: 0.009W
  ----
  opto: 5mA
  R9: 0.06W
  Con raspi-in = 5.13 y R10=1.55k+0.67k = 2.2k
  opto prende led
  A 11.39v valvula usa 0.35mA (sin conectar mide 12.06v)
  V(optoin-optoout)=1.54v
  V(Optoout-base)=8.72v
  V(Base-emisor)=0.73v
  Vled=1.9v
  VRled=8.75v
  Valvula se calienta bastante. Agua enfria?
  Rvalvula=28ohm
