# Fritzing sketch 1 valvula (saved by Fritzing 0.9.2b)
breadboards: 1

parts:
  12V = Power plug
  LED1 = LED - 3mm [color="Yellow (595nm)" package="3 mm [THT]"]
  R1 = Resistor [tolerance=±5% resistance=1.5k package=THT]
  Optocouple = IC, DIP package, 4 pins [chip_label=IC]
  R3 = Resistor [tolerance=±5% resistance=1.5k package=THT]
  R5 = Resistor [tolerance=±5% resistance=220 package=THT]
  Q1 = NPN-Transistor [package="TO92 [THT]"]
  Q2 = NPN-Transistor [package="TO92 [THT]"]
  Raspi_in = female pin header, 2 pins [form="♀ (female)"]
  R6 = Resistor [tolerance=±5% resistance=220 package=THT]
  L1 = Inductor [package="400 mil [THT]"]
  D1 = Rectifier Diode [part_number=1N4001 package="300 mil [THT]"]

nets:
  N1: 12V.VCC, R1.Pin_1, Optocouple.pin4, R3.Pin_1, L1.pin_0, D1.cathode
  GND: 12V.GND, Q1.E, Q2.E, Raspi_in.pin2
  N2: LED1.cathode, Optocouple.pin2, Q2.C
  N3: LED1.anode, R1.Pin_0
  N4: Optocouple.pin1, R3.Pin_0
  N5: Optocouple.pin3, R5.Pin_0
  N6: R5.Pin_1, Q1.B
  N7: Q1.C, L1.pin_1, D1.anode
  N8: Q2.B, R6.Pin_1
  N9: Raspi_in.pin1, R6.Pin_0
