# Fritzing sketch 2 valvulas (saved by Fritzing 0.9.2b)
circuit board: 6.01621cm x 3.10927cm
breadboards: 1

parts:
  12V2 = Power plug
  LED1 = LED - 3mm [color="Yellow (595nm)" package="3 mm [THT]"]
  R13 = Resistor [tolerance=±5% resistance=1.5k package=THT]
  Optocouple2 = IC, DIP package, 4 pins [chip_label=IC]
  R12 = Resistor [tolerance=±5% resistance=2.2k package=THT]
  R21 = Resistor [tolerance=±5% resistance=470 power=250mW package=THT]
  D1 = Rectifier Diode [part_number=1N4001 package="300 mil [THT]"]
  Valvula_12V1 = screw terminal, 2 pins
  Raspi_in = female pin header, 3 pins [form="♀ (female)"]
  Optocouple1 = IC, DIP package, 4 pins [chip_label=IC]
  R11 = Resistor [tolerance=±5% resistance=470 power=250mW package=THT]
  D2 = Rectifier Diode [part_number=1N4001 package="300 mil [THT]"]
  Valvula_12V2 = screw terminal, 2 pins
  LED2 = LED - 3mm [color="Yellow (595nm)" package="3 mm [THT]"]
  R23 = Resistor [tolerance=±5% resistance=1.5k package=THT]
  R22 = Resistor [tolerance=±5% resistance=2.2k package=THT]
  T1 = npn-Powertransistor [package="TO220 [THT]"]
  T2 = npn-Powertransistor [package="TO220 [THT]"]

nets:
  GND: 12V2.GND, T1.collector, T2.collector
  N1: 12V2.VCC, R13.Pin_1, Optocouple2.pin4, D1.cathode, Valvula_12V1.pin2, Optocouple1.pin4, D2.cathode, Valvula_12V2.pin2, R23.Pin_1
  N2: LED1.cathode, D1.anode, Valvula_12V1.pin1, T1.emitter
  N3: LED1.anode, R13.Pin_0
  N4: Optocouple2.pin1, R21.Pin_1
  N5: Optocouple2.pin2, Raspi_in.pin3, Optocouple1.pin2
  N6: Optocouple2.pin3, R22.Pin_0
  N7: R12.Pin_0, Optocouple1.pin3
  N8: R12.Pin_1, T1.base
  N9: R21.Pin_0, Raspi_in.pin2
  N10: Raspi_in.pin1, R11.Pin_0
  N11: Optocouple1.pin1, R11.Pin_1
  N12: D2.anode, Valvula_12V2.pin1, LED2.cathode, T2.emitter
  N13: LED2.anode, R23.Pin_0
  N14: R22.Pin_1, T2.base

notes:
  320mA
  7.2mA
  R8: 0.077W
  LED2: 0.009W
  ----
  opto: 5mA
  R9: 0.06W
