# Fritzing sketch panel domotica (saved by Fritzing 0.9.1b)
circuit board: 5.77022cm x 14.8333cm
breadboards: 1

parts:
  Power_plug1 = Power plug
  LED_ROJO = LED - 5mm [color="Red (633nm)" package="5 mm [THT]"]
  R3 = Resistor [tolerance=±5% resistance=10k package=THT]
  Q1 = NPN-Transistor [package="TO92 [THT]"]
  R5 = Resistor [tolerance=±5% resistance=220 package=THT]
  R2 = Resistor [tolerance=±5% resistance=100 package=THT]
  R4 = Resistor [tolerance=±5% resistance=10k package=THT]
  R6 = Resistor [tolerance=±5% resistance=10k package=THT]
  Q2 = NPN-Transistor [package="TO92 [THT]"]
  LED_VERDE = LED - 3mm [color="Green (565nm)" package="3 mm [THT]"]
  Q3 = NPN-Transistor [package="TO92 [THT]"]
  Q4 = NPN-Transistor [package="TO92 [THT]"]
  R7 = Resistor [tolerance=±5% resistance=100 package=THT]
  LED_VERDE1 = LED - 3mm [color="Green (565nm)" package="3 mm [THT]"]
  R8 = Resistor [tolerance=±5% resistance=10k package=THT]
  R9 = Resistor [tolerance=±5% resistance=10k package=THT]
  LED_ROJO1 = LED - 5mm [color="Red (633nm)" package="5 mm [THT]"]
  R10 = Resistor [tolerance=±5% resistance=220 package=THT]
  R11 = Resistor [tolerance=±5% resistance=10k package=THT]
  Q5 = NPN-Transistor [package="TO92 [THT]"]
  Q6 = NPN-Transistor [package="TO92 [THT]"]
  Q7 = NPN-Transistor [package="TO92 [THT]"]
  Q8 = NPN-Transistor [package="TO92 [THT]"]
  R12 = Resistor [tolerance=±5% resistance=100 package=THT]
  R13 = Resistor [tolerance=±5% resistance=100 package=THT]
  LED_VERDE2 = LED - 3mm [color="Green (565nm)" package="3 mm [THT]"]
  LED_VERDE3 = LED - 3mm [color="Green (565nm)" package="3 mm [THT]"]
  R14 = Resistor [tolerance=±5% resistance=10k package=THT]
  R15 = Resistor [tolerance=±5% resistance=10k package=THT]
  R16 = Resistor [tolerance=±5% resistance=10k package=THT]
  R17 = Resistor [tolerance=±5% resistance=10k package=THT]
  LED_ROJO2 = LED - 5mm [color="Red (633nm)" package="5 mm [THT]"]
  LED_ROJO3 = LED - 5mm [color="Red (633nm)" package="5 mm [THT]"]
  R18 = Resistor [tolerance=±5% resistance=220 package=THT]
  R19 = Resistor [tolerance=±5% resistance=220 package=THT]
  R20 = Resistor [tolerance=±5% resistance=10k package=THT]
  R21 = Resistor [tolerance=±5% resistance=10k package=THT]
  Q9 = NPN-Transistor [package="TO92 [THT]"]
  Q10 = NPN-Transistor [package="TO92 [THT]"]
  Q11 = NPN-Transistor [package="TO92 [THT]"]
  Q12 = NPN-Transistor [package="TO92 [THT]"]
  R22 = Resistor [tolerance=±5% resistance=100 package=THT]
  R23 = Resistor [tolerance=±5% resistance=100 package=THT]
  LED_VERDE4 = LED - 3mm [color="Green (565nm)" package="3 mm [THT]"]
  LED_VERDE5 = LED - 3mm [color="Green (565nm)" package="3 mm [THT]"]
  R24 = Resistor [tolerance=±5% resistance=10k package=THT]
  R25 = Resistor [tolerance=±5% resistance=10k package=THT]
  R26 = Resistor [tolerance=±5% resistance=10k package=THT]
  R27 = Resistor [tolerance=±5% resistance=10k package=THT]
  LED_ROJO4 = LED - 5mm [color="Red (633nm)" package="5 mm [THT]"]
  LED_ROJO5 = LED - 5mm [color="Red (633nm)" package="5 mm [THT]"]
  R28 = Resistor [tolerance=±5% resistance=220 package=THT]
  R29 = Resistor [tolerance=±5% resistance=220 package=THT]
  R30 = Resistor [tolerance=±5% resistance=10k package=THT]
  R31 = Resistor [tolerance=±5% resistance=10k package=THT]
  Q13 = NPN-Transistor [package="TO92 [THT]"]
  Q14 = NPN-Transistor [package="TO92 [THT]"]
  R32 = Resistor [tolerance=±5% resistance=100 package=THT]
  LED_VERDE6 = LED - 3mm [color="Green (565nm)" package="3 mm [THT]"]
  R33 = Resistor [tolerance=±5% resistance=10k package=THT]
  R34 = Resistor [tolerance=±5% resistance=10k package=THT]
  LED_ROJO6 = LED - 5mm [color="Red (633nm)" package="5 mm [THT]"]
  R35 = Resistor [tolerance=±5% resistance=220 package=THT]
  R36 = Resistor [tolerance=±5% resistance=10k package=THT]
  J6 = screw terminal, 2 pins
  J1 = Screw terminal - 2 pins [package=THT]
  J4 = Screw terminal - 2 pins [package=THT]
  J5 = screw terminal, 3 pins
  R37 = Resistor [tolerance=±5% resistance=220 package=THT]
  LED1 = LED - 3mm [color="Yellow (595nm)" package="3 mm [THT]"]
  J3 = Generic double row female header - 10 pins [form="♀ (female)" package=THT]

nets:
  GND: Power_plug1.GND, Q1.E, Q2.E, Q3.E, Q4.E, Q5.E, Q6.E, Q7.E, Q8.E, Q9.E, Q10.E, Q11.E, Q12.E, Q13.E, Q14.E, J6.pin2, R37.Pin_0, J3.pin2
  5V: Power_plug1.VCC, R5.Pin_1, R2.Pin_1, R7.Pin_1, R10.Pin_1, R12.Pin_1, R13.Pin_1, R18.Pin_1, R19.Pin_1, R22.Pin_1, R23.Pin_1, R28.Pin_1, R29.Pin_1, R32.Pin_1, R35.Pin_1, J6.pin1, LED1.anode
  N1: LED_ROJO.cathode, Q2.C
  N2: LED_ROJO.anode, R5.Pin_0
  N3: R3.Pin_0, Q1.C, LED_VERDE.cathode
  N4: R3.Pin_1, R4.Pin_1
  N5: Q1.B, R6.Pin_0
  N6: R2.Pin_0, LED_VERDE.anode
  N7: R4.Pin_0, Q2.B
  GPIO2: R6.Pin_1, J1.pin2, J3.pin10
  N8: Q3.B, R8.Pin_0
  N9: Q3.C, LED_ROJO1.cathode
  N10: Q4.B, R11.Pin_0
  N11: Q4.C, LED_VERDE1.cathode, R9.Pin_0
  N12: R7.Pin_0, LED_VERDE1.anode
  N13: R8.Pin_1, R9.Pin_1
  N14: LED_ROJO1.anode, R10.Pin_0
  GPIO3: R11.Pin_1, J1.pin1, J3.pin9
  N15: Q5.B, R14.Pin_0
  N16: Q5.C, LED_ROJO2.cathode
  N17: Q6.B, R15.Pin_0
  N18: Q6.C, LED_ROJO3.cathode
  N19: Q7.B, R20.Pin_0
  N20: Q7.C, LED_VERDE3.cathode, R16.Pin_0
  N21: Q8.B, R21.Pin_0
  N22: Q8.C, LED_VERDE2.cathode, R17.Pin_0
  N23: R12.Pin_0, LED_VERDE2.anode
  N24: R13.Pin_0, LED_VERDE3.anode
  N25: R14.Pin_1, R16.Pin_1
  N26: R15.Pin_1, R17.Pin_1
  N27: LED_ROJO2.anode, R18.Pin_0
  N28: LED_ROJO3.anode, R19.Pin_0
  GPIO4: R20.Pin_1, J4.pin2, J3.pin8
  GPIO17: R21.Pin_1, J4.pin1, J3.pin6
  N29: Q9.B, R24.Pin_0
  N30: Q9.C, LED_ROJO4.cathode
  N31: Q10.B, R25.Pin_0
  N32: Q10.C, LED_ROJO5.cathode
  N33: Q11.B, R30.Pin_0
  N34: Q11.C, LED_VERDE5.cathode, R26.Pin_0
  N35: Q12.B, R31.Pin_0
  N36: Q12.C, LED_VERDE4.cathode, R27.Pin_0
  N37: R22.Pin_0, LED_VERDE4.anode
  N38: R23.Pin_0, LED_VERDE5.anode
  N39: R24.Pin_1, R26.Pin_1
  N40: R25.Pin_1, R27.Pin_1
  N41: LED_ROJO4.anode, R28.Pin_0
  N42: LED_ROJO5.anode, R29.Pin_0
  GPIO18: R30.Pin_1, J5.pin3, J3.pin5
  GPIO15: R31.Pin_1, J5.pin2, J3.pin4
  N43: Q13.B, R33.Pin_0
  N44: Q13.C, LED_ROJO6.cathode
  N45: Q14.B, R36.Pin_0
  N46: Q14.C, LED_VERDE6.cathode, R34.Pin_0
  N47: R32.Pin_0, LED_VERDE6.anode
  N48: R33.Pin_1, R34.Pin_1
  N49: LED_ROJO6.anode, R35.Pin_0
  GPIO14: R36.Pin_1, J5.pin1, J3.pin3
  N50: R37.Pin_1, LED1.cathode

notes:
  MexotroniX
  Pins: 14|15|18|17|4|3|2  5V GND

custom parts:
  Generic double row female header - 10 pins: Generic double row female header
