# Fritzing sketch multi relay board x 4 (saved by Fritzing 0.9.1b)
circuit board: 6.56613cm x 7.70762cm
breadboards: 1

parts:
  R1 = Resistor [tolerance=±5% resistance=1k package=THT]
  Q1 = NPN-Transistor [package="TO92 [THT]"]
  R3 = Resistor [tolerance=±5% resistance=220 package=THT]
  U1 = TLP621 [package=THT]
  R4 = Resistor [tolerance=±5% resistance=1k package=THT]
  Q2 = NPN-Transistor [package="TO92 [THT]"]
  D1 = Rectifier Diode [part_number=1N4001 package="300 mil [THT]"]
  R7 = Resistor [tolerance=±5% resistance=180 package=THT]
  LED4 = LED - 5mm [color="Red (633nm)" package="5 mm [THT]"]
  J5 = male pin header, 1 pin [form="♂ (male)"]
  J4 = male pin header, 1 pin [form="♂ (male)"]
  J2 = screw terminal, 3 pins
  D2 = Rectifier Diode [part_number=1N4001 package="300 mil [THT]"]
  J9 = screw terminal, 3 pins
  R8 = Resistor [tolerance=±5% resistance=180 package=THT]
  LED5 = LED - 5mm [color="Red (633nm)" package="5 mm [THT]"]
  J14 = male pin header, 1 pin [form="♂ (male)"]
  J15 = male pin header, 1 pin [form="♂ (male)"]
  R9 = Resistor [tolerance=±5% resistance=1k package=THT]
  Q3 = NPN-Transistor [package="TO92 [THT]"]
  R10 = Resistor [tolerance=±5% resistance=220 package=THT]
  U2 = TLP621 [package=THT]
  R11 = Resistor [tolerance=±5% resistance=1k package=THT]
  Q4 = NPN-Transistor [package="TO92 [THT]"]
  J10 = female pin header, 1 pin [form="♀ (female)"]
  J11 = male pin header, 1 pin [form="♂ (male)"]
  J13 = male pin header, 1 pin [form="♂ (male)"]
  J12 = male alternating pin header, 1 pin [form="♂ (male)"]
  J16 = double row female pin header, 2 pins [form="♀ (female)"]
  J17 = female pin header, 1 pin [form="♀ (female)"]
  J6 = male alternating pin header, 1 pin [form="♂ (male)"]
  J7 = male pin header, 1 pin [form="♂ (male)"]
  J8 = male pin header, 1 pin [form="♂ (male)"]
  D3 = Rectifier Diode [part_number=1N4001 package="300 mil [THT]"]
  J18 = screw terminal, 3 pins
  R12 = Resistor [tolerance=±5% resistance=180 package=THT]
  LED6 = LED - 5mm [color="Red (633nm)" package="5 mm [THT]"]
  J19 = female pin header, 1 pin [form="♀ (female)"]
  J20 = male pin header, 1 pin [form="♂ (male)"]
  J21 = male alternating pin header, 1 pin [form="♂ (male)"]
  J22 = male pin header, 1 pin [form="♂ (male)"]
  J23 = male pin header, 1 pin [form="♂ (male)"]
  J24 = male pin header, 1 pin [form="♂ (male)"]
  R13 = Resistor [tolerance=±5% resistance=1k package=THT]
  Q5 = NPN-Transistor [package="TO92 [THT]"]
  R14 = Resistor [tolerance=±5% resistance=220 package=THT]
  U3 = TLP621 [package=THT]
  R15 = Resistor [tolerance=±5% resistance=1k package=THT]
  Q6 = NPN-Transistor [package="TO92 [THT]"]
  D4 = Rectifier Diode [part_number=1N4001 package="300 mil [THT]"]
  J25 = screw terminal, 3 pins
  R16 = Resistor [tolerance=±5% resistance=180 package=THT]
  LED7 = LED - 5mm [color="Red (633nm)" package="5 mm [THT]"]
  J26 = female pin header, 1 pin [form="♀ (female)"]
  J27 = male pin header, 1 pin [form="♂ (male)"]
  J28 = male alternating pin header, 1 pin [form="♂ (male)"]
  J29 = male pin header, 1 pin [form="♂ (male)"]
  J30 = male pin header, 1 pin [form="♂ (male)"]
  J31 = male pin header, 1 pin [form="♂ (male)"]
  R17 = Resistor [tolerance=±5% resistance=1k package=THT]
  Q7 = NPN-Transistor [package="TO92 [THT]"]
  R18 = Resistor [tolerance=±5% resistance=220 package=THT]
  U4 = TLP621 [package=THT]
  R19 = Resistor [tolerance=±5% resistance=1k package=THT]
  Q8 = NPN-Transistor [package="TO92 [THT]"]

nets:
  N1: R1.Pin_0, J17.pin1
  N2: R1.Pin_1, Q1.B
  GND: Q1.E, Q2.E, Q3.E, Q4.E, J16.pin2, Q5.E, Q6.E, Q7.E, Q8.E
  N3: Q1.C, R3.Pin_1, R7.Pin_0
  N4: R3.Pin_0, U1.Pin_2
  5V: U1.Pin_1, U1.Pin_4, D1.cathode, LED4.anode, J4.pin1, D2.cathode, LED5.anode, J14.pin1, U2.Pin_1, U2.Pin_4, J16.pin1, D3.cathode, LED6.anode, J23.pin1, U3.Pin_1, U3.Pin_4, D4.cathode, LED7.anode, J30.pin1, U4.Pin_1, U4.Pin_4
  N5: U1.Pin_3, R4.Pin_0
  N6: R4.Pin_1, Q2.B
  N7: Q2.C, D1.anode, J6.pin1
  N8: R7.Pin_1, LED4.cathode
  N9: J5.pin1, J2.pin2
  N10: J2.pin1, J8.pin1
  N11: J2.pin3, J7.pin1
  N12: D2.anode, Q4.C, J12.pin1
  N13: J9.pin1, J11.pin1
  N14: J9.pin2, J15.pin1
  N15: J9.pin3, J13.pin1
  N16: R8.Pin_0, Q3.C, R10.Pin_1
  N17: R8.Pin_1, LED5.cathode
  N18: R9.Pin_0, J10.pin1
  N19: R9.Pin_1, Q3.B
  N20: R10.Pin_0, U2.Pin_2
  N21: U2.Pin_3, R11.Pin_0
  N22: R11.Pin_1, Q4.B
  N23: D3.anode, J21.pin1, Q6.C
  N24: J18.pin1, J20.pin1
  N25: J18.pin2, J24.pin1
  N26: J18.pin3, J22.pin1
  N27: R12.Pin_0, Q5.C, R14.Pin_1
  N28: R12.Pin_1, LED6.cathode
  N29: J19.pin1, R13.Pin_0
  N30: R13.Pin_1, Q5.B
  N31: R14.Pin_0, U3.Pin_2
  N32: U3.Pin_3, R15.Pin_0
  N33: R15.Pin_1, Q6.B
  N34: D4.anode, J28.pin1, Q8.C
  N35: J25.pin1, J27.pin1
  N36: J25.pin2, J31.pin1
  N37: J25.pin3, J29.pin1
  N38: R16.Pin_0, Q7.C, R18.Pin_1
  N39: R16.Pin_1, LED7.cathode
  N40: J26.pin1, R17.Pin_0
  N41: R17.Pin_1, Q7.B
  N42: R18.Pin_0, U4.Pin_2
  N43: U4.Pin_3, R19.Pin_0
  N44: R19.Pin_1, Q8.B

notes:
  MexotroniX
