# Fritzing sketch relay board (saved by Fritzing 0.9.1b)
circuit board: 6.39591cm x 1.95964cm
breadboards: 1

parts:
  R1 = Resistor [tolerance=±5% resistance=1k package=THT]
  Q1 = NPN-Transistor [package="TO92 [THT]"]
  R3 = Resistor [tolerance=±5% resistance=220 package=THT]
  U1 = TLP621 [package=THT]
  R4 = Resistor [tolerance=±5% resistance=1k package=THT]
  Q2 = NPN-Transistor [package="TO92 [THT]"]
  D1 = Rectifier Diode [part_number=1N4001 package="300 mil [THT]"]
  R7 = Resistor [tolerance=±5% resistance=180 package=THT]
  LED4 = LED - 5mm [color="Red (633nm)" package="5 mm [THT]"]
  J3 = female pin header, 3 pins [form="♀ (female)"]
  J5 = male pin header, 1 pin [form="♂ (male)"]
  J4 = male pin header, 1 pin [form="♂ (male)"]
  J6 = male alternating pin header, 1 pin [form="♂ (male)"]
  J8 = male pin header, 1 pin [form="♂ (male)"]
  J7 = male pin header, 1 pin [form="♂ (male)"]
  J2 = screw terminal, 3 pins

nets:
  N1: R1.Pin_0, J3.pin2
  N2: R1.Pin_1, Q1.B
  GND: Q1.E, Q2.E, J3.pin1
  N3: Q1.C, R3.Pin_1, R7.Pin_0
  N4: R3.Pin_0, U1.Pin_2
  5V: U1.Pin_1, U1.Pin_4, D1.cathode, LED4.anode, J3.pin3, J4.pin1
  N5: U1.Pin_3, R4.Pin_0
  N6: R4.Pin_1, Q2.B
  N7: Q2.C, D1.anode, J6.pin1
  N8: R7.Pin_1, LED4.cathode
  N9: J5.pin1, J2.pin2
  N10: J8.pin1, J2.pin1
  N11: J7.pin1, J2.pin3

notes:
  MexotroniX
